# Fritzing sketch wiring (saved by Fritzing 0.9.0b)
breadboards: 1

parts:
  Деталь1 = Arduino Nano (Rev3.0)
  RHT1 = Humidity and Temperature Sensor RHT03
  Деталь2 = Barometric Pressure Sensor - BMP085 Breakout
  R1 = Resistor [tolerance=±5% resistance=1k package=THT]
  Деталь3 = Arduino Ethernet Shield (Rev3)

nets:
  GND: Деталь1.GND, RHT1.GND_2, Деталь2.GND, Деталь3.ICSP_MOSI
  N1: Деталь1.D3, RHT1.Data-signal, R1.Pin_1
  N2: Деталь1.D10, Деталь3.ETH_CS
  5V: Деталь1.5V, RHT1.Vcc, R1.Pin_0
  N3: Деталь1.A5, Деталь2.SCL
  N4: Деталь1.A4, Деталь2.SDA
  3V3: Деталь1.3V3, Деталь2.VCC

notes:
  1k
  SDA
  SCL
